// Logisim project minirv.circ as structural Verilog: 4 circuits, main circuit main
module main (
);

  wire comparator_1_eq, comparator_2_eq, pc_register_32_bit_1_out1, pc_register_32_bit_1_out2,
       pc_register_32_bit_1_out3, pc_register_32_bit_1_out4, pc_register_32_bit_1_out_41;
  wire [2:0] rom_32_bit_1_out_18;
  wire [6:0] rom_32_bit_1_out0;

  PC_Register_32_bit pc_register_32_bit_1 (
    .Out1(pc_register_32_bit_1_out1), .Out2(pc_register_32_bit_1_out2), .Out3(pc_register_32_bit_1_out3),
    .Out4(pc_register_32_bit_1_out4), .out_41(pc_register_32_bit_1_out_41));  // open: addr0, addr1, addr2, addr3, in_5, in_6, in_7, in_8, in_9, in_10, in_11, in_12, in_13, in_14, in_15, in_16, in_17, in_18, in_19, in_20, in_21, in_22, in_23, in_24, in_25, in_26, in_27, in_28, addr28, addr29, addr30, addr31, flag, EN, clk, Rst, out_42, out_43, out_44, out_45, out_46, out_47, out_48, out_49, out_50, out_51, out_52, out_53, out_54, out_55, out_56, out_57, out_58, out_59, out_60, out_61, out_62, out_63, out_64, Out28, Out29, Out30, Out31
  ROM_32_bit rom_32_bit_1 (
    .in_1(pc_register_32_bit_1_out1), .in_2(pc_register_32_bit_1_out2), .in_3(pc_register_32_bit_1_out3),
    .in_4(pc_register_32_bit_1_out4), .in_5(pc_register_32_bit_1_out_41), .Out0(rom_32_bit_1_out0[0]),
    .out_7(rom_32_bit_1_out0[1]), .out_8(rom_32_bit_1_out0[2]), .out_9(rom_32_bit_1_out0[3]),
    .out_10(rom_32_bit_1_out0[4]), .out_11(rom_32_bit_1_out0[5]), .out_12(rom_32_bit_1_out0[6]),
    .out_18(rom_32_bit_1_out_18[0]), .out_19(rom_32_bit_1_out_18[1]), .out_20(rom_32_bit_1_out_18[2]));  // open: Out7, out_14, out_15, out_16, out_17, Out15, out_22, out_23, out_24, out_25, out_26, out_27, out_28, Out23, out_30, out_31, out_32, out_33, out_34, out_35, out_36, Out31
  Comparator #(.mode("unsigned"), .width(7)) comparator_1 (
    .a(rom_32_bit_1_out0), .b(7'b0010011), .eq(comparator_1_eq));  // open: gt, lt
  Comparator #(.mode("unsigned"), .width(3)) comparator_2 (
    .a(rom_32_bit_1_out_18), .b(3'b000), .eq(comparator_2_eq));  // open: gt, lt
  // AND_Gate and_1 has open pins: in0=comparator_1_eq, in1=comparator_2_eq, out=open
  Bit_Extender #(.in_width(12), .out_width(32), .\type ("zero")) bit_extender_1 ();  // open: in, out
endmodule

module ROM_32_bit (
  input  in_1,
  input  in_2,
  input  in_3,
  input  in_4,
  input  in_5,
  output Out0,
  output out_7,
  output out_8,
  output out_9,
  output out_10,
  output out_11,
  output out_12,
  output Out7,
  output out_14,
  output out_15,
  output out_16,
  output out_17,
  output out_18,
  output out_19,
  output out_20,
  output Out15,
  output out_22,
  output out_23,
  output out_24,
  output out_25,
  output out_26,
  output out_27,
  output out_28,
  output Out23,
  output out_30,
  output out_31,
  output out_32,
  output out_33,
  output out_34,
  output out_35,
  output out_36,
  output Out31
);

  Multiplexer #(.select(5), .width(32)) multiplexer_1 (
    .in0(32'h108113),
    .out({Out31, out_36, out_35, out_34, out_33, out_32, out_31, out_30, Out23, out_28, out_27, out_26, out_25, out_24, out_23, out_22, Out15, out_20, out_19, out_18, out_17, out_16, out_15, out_14, Out7, out_12, out_11, out_10, out_9, out_8, out_7, Out0}),
    .sel({in_1, in_2, in_3, in_4, in_5}));  // open: in1, in2, in3, in4, in5, in6, in7, in8, in9, in10, in11, in12, in13, in14, in15, in16, in17, in18, in19, in20, in21, in22, in23, in24, in25, in26, in27, in28, in29, in30, in31
endmodule

module PC_Register_32_bit (
  input  addr0,
  input  addr1,
  input  addr2,
  input  addr3,
  input  in_5,
  input  in_6,
  input  in_7,
  input  in_8,
  input  in_9,
  input  in_10,
  input  in_11,
  input  in_12,
  input  in_13,
  input  in_14,
  input  in_15,
  input  in_16,
  input  in_17,
  input  in_18,
  input  in_19,
  input  in_20,
  input  in_21,
  input  in_22,
  input  in_23,
  input  in_24,
  input  in_25,
  input  in_26,
  input  in_27,
  input  in_28,
  input  addr28,
  input  addr29,
  input  addr30,
  input  addr31,
  input  flag,
  input  EN,
  input  clk,
  input  Rst,
  output Out1,
  output Out2,
  output Out3,
  output Out4,
  output out_41,
  output out_42,
  output out_43,
  output out_44,
  output out_45,
  output out_46,
  output out_47,
  output out_48,
  output out_49,
  output out_50,
  output out_51,
  output out_52,
  output out_53,
  output out_54,
  output out_55,
  output out_56,
  output out_57,
  output out_58,
  output out_59,
  output out_60,
  output out_61,
  output out_62,
  output out_63,
  output out_64,
  output Out28,
  output Out29,
  output Out30,
  output Out31
);

  wire [31:0] adder_1_out, and_1_out, and_2_out, or_1_out;
  wire [31:31] not_1_out;

  not not_1 (not_1_out[31], flag);
  assign and_1_out = {addr31, addr30, addr29, addr28, in_28, in_27, in_26, in_25, in_24, in_23, in_22, in_21, in_20, in_19, in_18, in_17, in_16, in_15, in_14, in_13, in_12, in_11, in_10, in_9, in_8, in_7, in_6, in_5, addr3, addr2, addr1, addr0} & {32{not_1_out[31]}};  // AND_Gate and_1, 32 bits wide
  assign or_1_out = and_1_out | and_2_out;  // OR_Gate or_1, 32 bits wide
  Register #(.width(32)) register_1 (
    .D(or_1_out), .en(EN), .clk(clk),
    .Q({Out31, Out30, Out29, Out28, out_64, out_63, out_62, out_61, out_60, out_59, out_58, out_57, out_56, out_55, out_54, out_53, out_52, out_51, out_50, out_49, out_48, out_47, out_46, out_45, out_44, out_43, out_42, out_41, Out4, Out3, Out2, Out1}),
    .clr(Rst));
  assign and_2_out = {32{flag}} & adder_1_out;  // AND_Gate and_2, 32 bits wide
  Adder #(.width(32)) adder_1 (
    .a(32'h1),
    .b({Out31, Out30, Out29, Out28, out_64, out_63, out_62, out_61, out_60, out_59, out_58, out_57, out_56, out_55, out_54, out_53, out_52, out_51, out_50, out_49, out_48, out_47, out_46, out_45, out_44, out_43, out_42, out_41, Out4, Out3, Out2, Out1}),
    .out(adder_1_out));  // open: cin, cout
endmodule

module RAM_32_32bit (
  input  R1addr0,
  input  R1addr1,
  input  R1addr2,
  input  R1addr3,
  input  R1addr4,
  input  clk,
  input  Rst,
  input  R2addr0,
  input  R2addr1,
  input  R2addr2,
  input  R2addr3,
  input  R2addr4,
  input  [31:0] Wdata,
  input  Waddr0,
  input  Waddr1,
  input  Waddr2,
  input  Waddr3,
  input  Waddr4,
  output [31:0] Read1,
  output [31:0] Read2
);

  wire demultiplexer_2_out1, demultiplexer_2_out2, demultiplexer_2_out3, demultiplexer_2_out4,
       demultiplexer_2_out5, demultiplexer_2_out6, demultiplexer_2_out7, demultiplexer_2_out8,
       demultiplexer_2_out9, demultiplexer_2_out10, demultiplexer_2_out11, demultiplexer_2_out12,
       demultiplexer_2_out13, demultiplexer_2_out14, demultiplexer_2_out15, demultiplexer_2_out16,
       demultiplexer_2_out17, demultiplexer_2_out18, demultiplexer_2_out19, demultiplexer_2_out20,
       demultiplexer_2_out21, demultiplexer_2_out22, demultiplexer_2_out23, demultiplexer_2_out24,
       demultiplexer_2_out25, demultiplexer_2_out26, demultiplexer_2_out27, demultiplexer_2_out28,
       demultiplexer_2_out29, demultiplexer_2_out30, demultiplexer_2_out31;
  wire [31:0] demultiplexer_1_out1, demultiplexer_1_out2, demultiplexer_1_out3, demultiplexer_1_out4,
       demultiplexer_1_out5, demultiplexer_1_out6, demultiplexer_1_out7, demultiplexer_1_out8,
       demultiplexer_1_out9, demultiplexer_1_out10, demultiplexer_1_out11, demultiplexer_1_out12,
       demultiplexer_1_out13, demultiplexer_1_out14, demultiplexer_1_out15, demultiplexer_1_out16,
       demultiplexer_1_out17, demultiplexer_1_out18, demultiplexer_1_out19, demultiplexer_1_out20,
       demultiplexer_1_out21, demultiplexer_1_out22, demultiplexer_1_out23, demultiplexer_1_out24,
       demultiplexer_1_out25, demultiplexer_1_out26, demultiplexer_1_out27, demultiplexer_1_out28,
       demultiplexer_1_out29, demultiplexer_1_out30, demultiplexer_1_out31, register_1_q, register_2_q,
       register_3_q, register_4_q, register_5_q, register_6_q, register_7_q, register_8_q, register_9_q,
       register_10_q, register_11_q, register_12_q, register_13_q, register_14_q, register_15_q,
       register_16_q, register_17_q, register_18_q, register_19_q, register_20_q, register_21_q,
       register_22_q, register_23_q, register_24_q, register_25_q, register_26_q, register_27_q,
       register_28_q, register_29_q, register_30_q, register_31_q, register_32_q;

  Demultiplexer #(.select(5), .width(32)) demultiplexer_1 (
    .out1(demultiplexer_1_out1), .out2(demultiplexer_1_out2), .out3(demultiplexer_1_out3),
    .out4(demultiplexer_1_out4), .out5(demultiplexer_1_out5), .out6(demultiplexer_1_out6),
    .out7(demultiplexer_1_out7), .out8(demultiplexer_1_out8), .out9(demultiplexer_1_out9),
    .out10(demultiplexer_1_out10), .out11(demultiplexer_1_out11), .out12(demultiplexer_1_out12),
    .out13(demultiplexer_1_out13), .out14(demultiplexer_1_out14), .out15(demultiplexer_1_out15),
    .out16(demultiplexer_1_out16), .out17(demultiplexer_1_out17), .out18(demultiplexer_1_out18),
    .out19(demultiplexer_1_out19), .out20(demultiplexer_1_out20), .out21(demultiplexer_1_out21),
    .out22(demultiplexer_1_out22), .out23(demultiplexer_1_out23), .out24(demultiplexer_1_out24),
    .out25(demultiplexer_1_out25), .out26(demultiplexer_1_out26), .out27(demultiplexer_1_out27),
    .out28(demultiplexer_1_out28), .out29(demultiplexer_1_out29), .out30(demultiplexer_1_out30),
    .out31(demultiplexer_1_out31), .in(Wdata), .sel({Waddr4, Waddr3, Waddr2, Waddr1, Waddr0}));  // open: out0
  Register #(.width(32)) register_1 (.D({32{1'b0}}), .clk(clk), .Q(register_1_q), .clr(Rst));  // open: en
  Register #(.width(32)) register_2 (
    .D(demultiplexer_1_out1), .en(demultiplexer_2_out1), .clk(clk), .Q(register_2_q), .clr(Rst));
  Register #(.width(32)) register_3 (
    .D(demultiplexer_1_out2), .en(demultiplexer_2_out2), .clk(clk), .Q(register_3_q), .clr(Rst));
  Register #(.width(32)) register_4 (
    .D(demultiplexer_1_out3), .en(demultiplexer_2_out3), .clk(clk), .Q(register_4_q), .clr(Rst));
  Register #(.width(32)) register_5 (
    .D(demultiplexer_1_out16), .en(demultiplexer_2_out16), .clk(clk), .Q(register_5_q), .clr(Rst));
  Register #(.width(32)) register_6 (
    .D(demultiplexer_1_out17), .en(demultiplexer_2_out17), .clk(clk), .Q(register_6_q), .clr(Rst));
  Register #(.width(32)) register_7 (
    .D(demultiplexer_1_out18), .en(demultiplexer_2_out18), .clk(clk), .Q(register_7_q), .clr(Rst));
  Register #(.width(32)) register_8 (
    .D(demultiplexer_1_out19), .en(demultiplexer_2_out19), .clk(clk), .Q(register_8_q), .clr(Rst));
  Demultiplexer #(.select(5)) demultiplexer_2 (
    .out1(demultiplexer_2_out1), .out2(demultiplexer_2_out2), .out3(demultiplexer_2_out3),
    .out4(demultiplexer_2_out4), .out5(demultiplexer_2_out5), .out6(demultiplexer_2_out6),
    .out7(demultiplexer_2_out7), .out8(demultiplexer_2_out8), .out9(demultiplexer_2_out9),
    .out10(demultiplexer_2_out10), .out11(demultiplexer_2_out11), .out12(demultiplexer_2_out12),
    .out13(demultiplexer_2_out13), .out14(demultiplexer_2_out14), .out15(demultiplexer_2_out15),
    .out16(demultiplexer_2_out16), .out17(demultiplexer_2_out17), .out18(demultiplexer_2_out18),
    .out19(demultiplexer_2_out19), .out20(demultiplexer_2_out20), .out21(demultiplexer_2_out21),
    .out22(demultiplexer_2_out22), .out23(demultiplexer_2_out23), .out24(demultiplexer_2_out24),
    .out25(demultiplexer_2_out25), .out26(demultiplexer_2_out26), .out27(demultiplexer_2_out27),
    .out28(demultiplexer_2_out28), .out29(demultiplexer_2_out29), .out30(demultiplexer_2_out30),
    .out31(demultiplexer_2_out31), .in(1'b1), .sel({Waddr4, Waddr3, Waddr2, Waddr1, Waddr0}));  // open: out0
  Register #(.width(32)) register_9 (
    .D(demultiplexer_1_out4), .en(demultiplexer_2_out4), .clk(clk), .Q(register_9_q), .clr(Rst));
  Register #(.width(32)) register_10 (
    .D(demultiplexer_1_out5), .en(demultiplexer_2_out5), .clk(clk), .Q(register_10_q), .clr(Rst));
  Register #(.width(32)) register_11 (
    .D(demultiplexer_1_out6), .en(demultiplexer_2_out6), .clk(clk), .Q(register_11_q), .clr(Rst));
  Register #(.width(32)) register_12 (
    .D(demultiplexer_1_out7), .en(demultiplexer_2_out7), .clk(clk), .Q(register_12_q), .clr(Rst));
  Register #(.width(32)) register_13 (
    .D(demultiplexer_1_out20), .en(demultiplexer_2_out20), .clk(clk), .Q(register_13_q), .clr(Rst));
  Register #(.width(32)) register_14 (
    .D(demultiplexer_1_out21), .en(demultiplexer_2_out21), .clk(clk), .Q(register_14_q), .clr(Rst));
  Register #(.width(32)) register_15 (
    .D(demultiplexer_1_out22), .en(demultiplexer_2_out22), .clk(clk), .Q(register_15_q), .clr(Rst));
  Register #(.width(32)) register_16 (
    .D(demultiplexer_1_out23), .en(demultiplexer_2_out23), .clk(clk), .Q(register_16_q), .clr(Rst));
  Register #(.width(32)) register_17 (
    .D(demultiplexer_1_out8), .en(demultiplexer_2_out8), .clk(clk), .Q(register_17_q), .clr(Rst));
  Register #(.width(32)) register_18 (
    .D(demultiplexer_1_out9), .en(demultiplexer_2_out9), .clk(clk), .Q(register_18_q), .clr(Rst));
  Register #(.width(32)) register_19 (
    .D(demultiplexer_1_out10), .en(demultiplexer_2_out10), .clk(clk), .Q(register_19_q), .clr(Rst));
  Register #(.width(32)) register_20 (
    .D(demultiplexer_1_out11), .en(demultiplexer_2_out11), .clk(clk), .Q(register_20_q), .clr(Rst));
  Register #(.width(32)) register_21 (
    .D(demultiplexer_1_out24), .en(demultiplexer_2_out24), .clk(clk), .Q(register_21_q), .clr(Rst));
  Register #(.width(32)) register_22 (
    .D(demultiplexer_1_out25), .en(demultiplexer_2_out25), .clk(clk), .Q(register_22_q), .clr(Rst));
  Register #(.width(32)) register_23 (
    .D(demultiplexer_1_out26), .en(demultiplexer_2_out26), .clk(clk), .Q(register_23_q), .clr(Rst));
  Register #(.width(32)) register_24 (
    .D(demultiplexer_1_out27), .en(demultiplexer_2_out27), .clk(clk), .Q(register_24_q), .clr(Rst));
  Register #(.width(32)) register_25 (
    .D(demultiplexer_1_out12), .en(demultiplexer_2_out12), .clk(clk), .Q(register_25_q), .clr(Rst));
  Register #(.width(32)) register_26 (
    .D(demultiplexer_1_out13), .en(demultiplexer_2_out13), .clk(clk), .Q(register_26_q), .clr(Rst));
  Register #(.width(32)) register_27 (
    .D(demultiplexer_1_out14), .en(demultiplexer_2_out14), .clk(clk), .Q(register_27_q), .clr(Rst));
  Register #(.width(32)) register_28 (
    .D(demultiplexer_1_out15), .en(demultiplexer_2_out15), .clk(clk), .Q(register_28_q), .clr(Rst));
  Register #(.width(32)) register_29 (
    .D(demultiplexer_1_out28), .en(demultiplexer_2_out28), .clk(clk), .Q(register_29_q), .clr(Rst));
  Register #(.width(32)) register_30 (
    .D(demultiplexer_1_out29), .en(demultiplexer_2_out29), .clk(clk), .Q(register_30_q), .clr(Rst));
  Register #(.width(32)) register_31 (
    .D(demultiplexer_1_out30), .en(demultiplexer_2_out30), .clk(clk), .Q(register_31_q), .clr(Rst));
  Register #(.width(32)) register_32 (
    .D(demultiplexer_1_out31), .en(demultiplexer_2_out31), .clk(clk), .Q(register_32_q), .clr(Rst));
  Multiplexer #(.select(5), .width(32)) multiplexer_1 (
    .in0(register_1_q), .in1(register_2_q), .in2(register_3_q), .in3(register_4_q), .in4(register_9_q),
    .in5(register_10_q), .in6(register_11_q), .in7(register_12_q), .in8(register_17_q), .in9(register_18_q),
    .in10(register_19_q), .in11(register_20_q), .in12(register_25_q), .in13(register_26_q),
    .in14(register_27_q), .in15(register_28_q), .in16(register_5_q), .in17(register_6_q),
    .in18(register_7_q), .in19(register_8_q), .in20(register_13_q), .in21(register_14_q),
    .in22(register_15_q), .in23(register_16_q), .in24(register_21_q), .in25(register_22_q),
    .in26(register_23_q), .in27(register_24_q), .in28(register_29_q), .in29(register_30_q),
    .in30(register_31_q), .in31(register_32_q), .out(Read1),
    .sel({R1addr4, R1addr3, R1addr2, R1addr1, R1addr0}));
  Multiplexer #(.select(5), .width(32)) multiplexer_2 (
    .in0(register_1_q), .in1(register_2_q), .in2(register_3_q), .in3(register_4_q), .in4(register_9_q),
    .in5(register_10_q), .in6(register_11_q), .in7(register_12_q), .in8(register_17_q), .in9(register_18_q),
    .in10(register_19_q), .in11(register_20_q), .in12(register_25_q), .in13(register_26_q),
    .in14(register_27_q), .in15(register_28_q), .in16(register_5_q), .in17(register_6_q),
    .in18(register_7_q), .in19(register_8_q), .in20(register_13_q), .in21(register_14_q),
    .in22(register_15_q), .in23(register_16_q), .in24(register_21_q), .in25(register_22_q),
    .in26(register_23_q), .in27(register_24_q), .in28(register_29_q), .in29(register_30_q),
    .in30(register_31_q), .in31(register_32_q), .out(Read2),
    .sel({R2addr4, R2addr3, R2addr2, R2addr1, R2addr0}));

  // Notes on the sheet:
  //   Wdata: initial=0x80000000
  //   Write
  //   Read1
  //   Read2
endmodule
